// Logisim project rv32i_single_cycle_cpu.circ as structural Verilog: 11 circuits, main circuit CPU_Top
// ALU_RESULT
module ALU (
  input  [31:0] B,
  input  [31:0] A,
  input  [1:0] ALU_CONTROL,
  output [31:0] ALU_result,
  output ZERO
);

  wire [31:0] adder_1_out, and_1_out, or_1_out, subtractor_1_out;

  Adder #(.width(32)) adder_1 (.a(A), .b(B), .out(adder_1_out));  // open: cin, cout
  Subtractor #(.width(32)) subtractor_1 (.a(A), .b(B), .out(subtractor_1_out));  // open: bin, bout
  Multiplexer #(.select(2), .width(32), .enable("false")) multiplexer_1 (
    .in0(adder_1_out), .in1(subtractor_1_out), .in2(or_1_out), .in3(and_1_out), .out(ALU_result),
    .sel(ALU_CONTROL));
  // Probe on ALU_result
  assign or_1_out = B | A;  // OR_Gate or_1, 32 bits wide
  Comparator #(.width(32)) comparator_1 (.a(ALU_result), .b({32{1'b0}}), .eq(ZERO));  // open: gt, lt
  assign and_1_out = B & A;  // AND_Gate and_1, 32 bits wide
endmodule

module Register_File (
  input  [31:0] write_data,
  input  clock,
  input  reg_write,
  input  [4:0] read_address_1,
  input  [4:0] write_address,
  input  [4:0] read_address_2,
  output [31:0] read_data_1,
  output [31:0] read_data_2
);

  wire and_1_out, and_2_out, and_3_out, and_4_out, and_5_out, and_6_out, and_7_out, and_8_out, and_9_out,
       and_10_out, and_11_out, and_12_out, and_13_out, and_14_out, and_15_out, and_16_out, and_17_out,
       and_18_out, and_19_out, and_20_out, and_21_out, and_22_out, and_23_out, and_24_out, and_25_out,
       and_26_out, and_27_out, and_28_out, and_29_out, and_30_out, and_31_out, decoder_1_out1,
       decoder_1_out2, decoder_1_out3, decoder_1_out4, decoder_1_out5, decoder_1_out6, decoder_1_out7,
       decoder_1_out8, decoder_1_out9, decoder_1_out10, decoder_1_out11, decoder_1_out12, decoder_1_out13,
       decoder_1_out14, decoder_1_out15, decoder_1_out16, decoder_1_out17, decoder_1_out18, decoder_1_out19,
       decoder_1_out20, decoder_1_out21, decoder_1_out22, decoder_1_out23, decoder_1_out24, decoder_1_out25,
       decoder_1_out26, decoder_1_out27, decoder_1_out28, decoder_1_out29, decoder_1_out30, decoder_1_out31;
  wire [31:0] register_1_q, register_2_q, register_3_q, register_4_q, register_5_q, register_6_q,
       register_7_q, register_8_q, register_9_q, register_10_q, register_11_q, register_12_q, register_13_q,
       register_14_q, register_15_q, register_16_q, register_17_q, register_18_q, register_19_q,
       register_20_q, register_21_q, register_22_q, register_23_q, register_24_q, register_25_q,
       register_26_q, register_27_q, register_28_q, register_29_q, register_30_q, register_31_q;

  Decoder #(.select(5), .enable("false")) decoder_1 (
    .out1(decoder_1_out1), .out2(decoder_1_out2), .out3(decoder_1_out3), .out4(decoder_1_out4),
    .out5(decoder_1_out5), .out6(decoder_1_out6), .out7(decoder_1_out7), .out8(decoder_1_out8),
    .out9(decoder_1_out9), .out10(decoder_1_out10), .out11(decoder_1_out11), .out12(decoder_1_out12),
    .out13(decoder_1_out13), .out14(decoder_1_out14), .out15(decoder_1_out15), .out16(decoder_1_out16),
    .out17(decoder_1_out17), .out18(decoder_1_out18), .out19(decoder_1_out19), .out20(decoder_1_out20),
    .out21(decoder_1_out21), .out22(decoder_1_out22), .out23(decoder_1_out23), .out24(decoder_1_out24),
    .out25(decoder_1_out25), .out26(decoder_1_out26), .out27(decoder_1_out27), .out28(decoder_1_out28),
    .out29(decoder_1_out29), .out30(decoder_1_out30), .out31(decoder_1_out31), .sel(write_address));  // open: out0
  and and_1 (and_1_out, reg_write, decoder_1_out1);
  and and_2 (and_2_out, reg_write, decoder_1_out2);
  and and_3 (and_3_out, reg_write, decoder_1_out3);
  and and_4 (and_4_out, reg_write, decoder_1_out4);
  and and_5 (and_5_out, reg_write, decoder_1_out5);
  and and_6 (and_6_out, reg_write, decoder_1_out6);
  and and_7 (and_7_out, reg_write, decoder_1_out7);
  and and_8 (and_8_out, reg_write, decoder_1_out8);
  and and_9 (and_9_out, reg_write, decoder_1_out9);
  and and_10 (and_10_out, reg_write, decoder_1_out10);
  and and_11 (and_11_out, reg_write, decoder_1_out11);
  and and_12 (and_12_out, reg_write, decoder_1_out12);
  and and_13 (and_13_out, reg_write, decoder_1_out13);
  and and_14 (and_14_out, reg_write, decoder_1_out14);
  and and_15 (and_15_out, reg_write, decoder_1_out15);
  and and_16 (and_16_out, reg_write, decoder_1_out16);
  and and_17 (and_17_out, reg_write, decoder_1_out17);
  and and_18 (and_18_out, reg_write, decoder_1_out18);
  and and_19 (and_19_out, reg_write, decoder_1_out19);
  and and_20 (and_20_out, reg_write, decoder_1_out20);
  and and_21 (and_21_out, reg_write, decoder_1_out21);
  and and_22 (and_22_out, reg_write, decoder_1_out22);
  and and_23 (and_23_out, reg_write, decoder_1_out23);
  and and_24 (and_24_out, reg_write, decoder_1_out24);
  and and_25 (and_25_out, reg_write, decoder_1_out25);
  and and_26 (and_26_out, reg_write, decoder_1_out26);
  and and_27 (and_27_out, reg_write, decoder_1_out27);
  and and_28 (and_28_out, reg_write, decoder_1_out28);
  and and_29 (and_29_out, reg_write, decoder_1_out29);
  and and_30 (and_30_out, reg_write, decoder_1_out30);
  and and_31 (and_31_out, reg_write, decoder_1_out31);
  Register #(.width(32)) register_1 (.D(write_data), .en(and_1_out), .Q(register_1_q), .clk(clock));  // open: clr
  Register #(.width(32)) register_2 (.D(write_data), .en(and_2_out), .Q(register_2_q), .clk(clock));  // open: clr
  Register #(.width(32)) register_3 (.D(write_data), .en(and_3_out), .Q(register_3_q), .clk(clock));  // open: clr
  Register #(.width(32)) register_4 (.D(write_data), .en(and_4_out), .Q(register_4_q), .clk(clock));  // open: clr
  Register #(.width(32)) register_5 (.D(write_data), .en(and_5_out), .Q(register_5_q), .clk(clock));  // open: clr
  Register #(.width(32)) register_6 (.D(write_data), .en(and_6_out), .Q(register_6_q), .clk(clock));  // open: clr
  Register #(.width(32)) register_7 (.D(write_data), .en(and_7_out), .Q(register_7_q), .clk(clock));  // open: clr
  Register #(.width(32)) register_8 (.D(write_data), .en(and_8_out), .Q(register_8_q), .clk(clock));  // open: clr
  Register #(.width(32)) register_9 (.D(write_data), .en(and_9_out), .Q(register_9_q), .clk(clock));  // open: clr
  Register #(.width(32)) register_10 (.D(write_data), .en(and_10_out), .Q(register_10_q), .clk(clock));  // open: clr
  Register #(.width(32)) register_11 (.D(write_data), .en(and_11_out), .Q(register_11_q), .clk(clock));  // open: clr
  Register #(.width(32)) register_12 (.D(write_data), .en(and_12_out), .Q(register_12_q), .clk(clock));  // open: clr
  Register #(.width(32)) register_13 (.D(write_data), .en(and_13_out), .Q(register_13_q), .clk(clock));  // open: clr
  Register #(.width(32)) register_14 (.D(write_data), .en(and_14_out), .Q(register_14_q), .clk(clock));  // open: clr
  Register #(.width(32)) register_15 (.D(write_data), .en(and_15_out), .Q(register_15_q), .clk(clock));  // open: clr
  Register #(.width(32)) register_16 (.D(write_data), .en(and_16_out), .Q(register_16_q), .clk(clock));  // open: clr
  Register #(.width(32)) register_17 (.D(write_data), .en(and_17_out), .Q(register_17_q), .clk(clock));  // open: clr
  Register #(.width(32)) register_18 (.D(write_data), .en(and_18_out), .Q(register_18_q), .clk(clock));  // open: clr
  Register #(.width(32)) register_19 (.D(write_data), .en(and_19_out), .Q(register_19_q), .clk(clock));  // open: clr
  Register #(.width(32)) register_20 (.D(write_data), .en(and_20_out), .Q(register_20_q), .clk(clock));  // open: clr
  Register #(.width(32)) register_21 (.D(write_data), .en(and_21_out), .Q(register_21_q), .clk(clock));  // open: clr
  Register #(.width(32)) register_22 (.D(write_data), .en(and_22_out), .Q(register_22_q), .clk(clock));  // open: clr
  Register #(.width(32)) register_23 (.D(write_data), .en(and_23_out), .Q(register_23_q), .clk(clock));  // open: clr
  Register #(.width(32)) register_24 (.D(write_data), .en(and_24_out), .Q(register_24_q), .clk(clock));  // open: clr
  Register #(.width(32)) register_25 (.D(write_data), .en(and_25_out), .Q(register_25_q), .clk(clock));  // open: clr
  Register #(.width(32)) register_26 (.D(write_data), .en(and_26_out), .Q(register_26_q), .clk(clock));  // open: clr
  Register #(.width(32)) register_27 (.D(write_data), .en(and_27_out), .Q(register_27_q), .clk(clock));  // open: clr
  Register #(.width(32)) register_28 (.D(write_data), .en(and_28_out), .Q(register_28_q), .clk(clock));  // open: clr
  Register #(.width(32)) register_29 (.D(write_data), .en(and_29_out), .Q(register_29_q), .clk(clock));  // open: clr
  Register #(.width(32)) register_30 (.D(write_data), .en(and_30_out), .Q(register_30_q), .clk(clock));  // open: clr
  Register #(.width(32)) register_31 (.D(write_data), .en(and_31_out), .Q(register_31_q), .clk(clock));  // open: clr
  Multiplexer #(.select(5), .width(32), .enable("false")) multiplexer_1 (
    .in0({32{1'b0}}), .in1(register_1_q), .in2(register_2_q), .in3(register_3_q), .in4(register_4_q),
    .in5(register_5_q), .in6(register_6_q), .in7(register_7_q), .in8(register_8_q), .in9(register_9_q),
    .in10(register_10_q), .in11(register_11_q), .in12(register_12_q), .in13(register_13_q),
    .in14(register_14_q), .in15(register_15_q), .in16(register_16_q), .in17(register_17_q),
    .in18(register_18_q), .in19(register_19_q), .in20(register_20_q), .in21(register_21_q),
    .in22(register_22_q), .in23(register_23_q), .in24(register_24_q), .in25(register_25_q),
    .in26(register_26_q), .in27(register_27_q), .in28(register_28_q), .in29(register_29_q),
    .in30(register_30_q), .in31(register_31_q), .out(read_data_1), .sel(read_address_1));
  Multiplexer #(.select(5), .width(32), .enable("false")) multiplexer_2 (
    .in0({32{1'b0}}), .in1(register_1_q), .in2(register_2_q), .in3(register_3_q), .in4(register_4_q),
    .in5(register_5_q), .in6(register_6_q), .in7(register_7_q), .in8(register_8_q), .in9(register_9_q),
    .in10(register_10_q), .in11(register_11_q), .in12(register_12_q), .in13(register_13_q),
    .in14(register_14_q), .in15(register_15_q), .in16(register_16_q), .in17(register_17_q),
    .in18(register_18_q), .in19(register_19_q), .in20(register_20_q), .in21(register_21_q),
    .in22(register_22_q), .in23(register_23_q), .in24(register_24_q), .in25(register_25_q),
    .in26(register_26_q), .in27(register_27_q), .in28(register_28_q), .in29(register_29_q),
    .in30(register_30_q), .in31(register_31_q), .out(read_data_2), .sel(read_address_2));
endmodule

module program_counter (
  input  [31:0] next_pc,
  input  clock,
  output [31:0] pc
);

  Register #(.width(32)) u_PC (.D(next_pc), .en(1'b1), .Q(pc), .clk(clock));  // open: clr
endmodule

module Instruction_Memory (
  input  [4:0] instruction_address,
  output [31:0] instruction
);

  ROM #(.addrWidth(5), .dataWidth(32)) rom_1 (.addr(instruction_address), .data(instruction), .sel(1'b1));
  // Probe on instruction

  // Notes on the sheet:
  //   contents of rom_1 (hex, n*v repeats v):
  //   a00393 1400493 938133
endmodule

module Instruction_splitter (
  input  [31:0] instruction,
  output [6:0] opcode,
  output [4:0] rd,
  output [2:0] funct3,
  output [4:0] rs1,
  output [4:0] rs2,
  output [6:0] funct7
);


  assign funct3 = instruction[14:12];
  assign funct7 = instruction[31:25];
  assign opcode = instruction[6:0];
  assign rd = instruction[11:7];
  assign rs1 = instruction[19:15];
  assign rs2 = instruction[24:20];
endmodule

module Immediate_Generator (
  input  [31:0] instruction,
  input  [1:0] imm_sel,
  output [31:0] immediate
);

  wire [31:0] bit_extender_1_out, bit_extender_2_out, bit_extender_3_out, bit_extender_4_out;

  assign bit_extender_1_out = {{11{instruction[31]}}, {instruction[31], instruction[19:12], instruction[20], instruction[30:21], 1'b0}};  // Bit_Extender bit_extender_1
  assign bit_extender_2_out = {{19{instruction[31]}}, {instruction[31], instruction[7], instruction[30:25], instruction[11:8], 1'b0}};  // Bit_Extender bit_extender_2
  assign bit_extender_3_out = {{20{instruction[31]}}, {instruction[31:25], instruction[11:7]}};  // Bit_Extender bit_extender_3
  assign bit_extender_4_out = {{20{instruction[31]}}, instruction[31:20]};  // Bit_Extender bit_extender_4
  Multiplexer #(.select(2), .width(32), .enable("false")) multiplexer_1 (
    .in0(bit_extender_4_out), .in1(bit_extender_3_out), .in2(bit_extender_2_out), .in3(bit_extender_1_out),
    .out(immediate), .sel(imm_sel));
endmodule

module Main_control (
  input  [6:0] opcode,
  output RegWrite,
  output is_R_type,
  output ALUSrc,
  output is_ADDI,
  output memread,
  output is_LW,
  output MemWrite,
  output is_SW,
  output Branch,
  output is_BEQ,
  output jump,
  output is_JAL,
  output [1:0] ResultSrc,
  output [1:0] immsel,
  output [1:0] ALU_OP
);

  Comparator #(.width(7)) comparator_1 (.a(opcode), .b(7'b0110011), .eq(ALU_OP[1]));  // open: gt, lt
  Comparator #(.width(7)) comparator_2 (.a(opcode), .b(7'b0010011), .eq(is_ADDI));  // open: gt, lt
  Comparator #(.width(7)) comparator_3 (.a(opcode), .b(7'b0000011), .eq(is_LW));  // open: gt, lt
  Comparator #(.width(7)) comparator_4 (.a(opcode), .b(7'b0100011), .eq(is_SW));  // open: gt, lt
  Comparator #(.width(7)) comparator_5 (.a(opcode), .b(7'b1100011), .eq(ALU_OP[0]));  // open: gt, lt
  Comparator #(.width(7)) comparator_6 (.a(opcode), .b(7'b1101111), .eq(is_JAL));  // open: gt, lt
  or or_1 (RegWrite, ALU_OP[1], is_ADDI, is_LW, is_JAL);
  or or_2 (ALUSrc, is_ADDI, is_SW, is_LW);
  or or_3 (immsel[0], is_SW, is_JAL);
  or or_4 (immsel[1], is_JAL, ALU_OP[0]);

  assign Branch = ALU_OP[0];
  assign is_BEQ = ALU_OP[0];
  assign is_R_type = ALU_OP[1];
  assign jump = is_JAL;
  assign memread = is_LW;
  assign MemWrite = is_SW;
  assign ResultSrc = {is_JAL, is_LW};
endmodule

module ALU_Control (
  input  [1:0] ALUOp,
  input  [2:0] funct3,
  input  [6:0] funct7,
  output R_SUB,
  output ALUControl_0,
  output [1:0] ALU_Control,
  output R_AND,
  output ALUControl_1,
  output R_OR
);

  wire comparator_1_eq, comparator_2_eq, comparator_3_eq, comparator_4_eq, comparator_5_eq, comparator_6_eq,
       comparator_7_eq;

  Comparator #(.width(2)) comparator_1 (.a(ALUOp), .b(2'b01), .eq(comparator_1_eq));  // open: gt, lt
  Comparator #(.width(2)) comparator_2 (.a(ALUOp), .b(2'b10), .eq(comparator_2_eq));  // open: gt, lt
  Comparator #(.width(3)) comparator_3 (.a(funct3), .b(3'b000), .eq(comparator_3_eq));  // open: gt, lt
  Comparator #(.width(3)) comparator_4 (.a(funct3), .b(3'b110), .eq(comparator_4_eq));  // open: gt, lt
  Comparator #(.width(3)) comparator_5 (.a(funct3), .b(3'b111), .eq(comparator_5_eq));  // open: gt, lt
  Comparator #(.width(7)) comparator_6 (.a(funct7), .b({7{1'b0}}), .eq(comparator_6_eq));  // open: gt, lt
  Comparator #(.width(7)) comparator_7 (.a(funct7), .b(7'b0100000), .eq(comparator_7_eq));  // open: gt, lt
  and and_1 (R_SUB, comparator_2_eq, comparator_3_eq, comparator_7_eq);
  and and_2 (R_AND, comparator_2_eq, comparator_5_eq, comparator_6_eq);
  and and_3 (R_OR, comparator_4_eq, comparator_2_eq, comparator_6_eq);
  or or_1 (ALU_Control[0], comparator_1_eq, R_SUB, R_OR);
  or or_2 (ALU_Control[1], R_AND, R_OR);

  assign ALUControl_0 = ALU_Control[0];
  assign ALUControl_1 = ALU_Control[1];
endmodule

module data_memory (
  input  [31:0] address,
  input  [31:0] write_data,
  input  Memwrite,
  input  Memread,
  input  clock,
  output [31:0] read_data
);

  wire or_1_out;

  or or_1 (or_1_out, Memwrite, Memread);
  RAM #(.addrWidth(5), .dataWidth(32), .bus("separate")) ram_1 (
    .addr(address[6:2]), .din(write_data), .data(read_data), .str(Memwrite), .sel(or_1_out), .clk(clock),
    .ld(Memread), .clr(1'b0));
endmodule

module Branch_Jump_Logic (
  input  [31:0] pc,
  input  [31:0] immediate,
  input  Branch,
  input  zero,
  input  jump,
  output [31:0] pc_plus4,
  output [31:0] next_pc
);

  wire and_1_out, or_1_out;
  wire [31:0] adder_2_out;

  and and_1 (and_1_out, Branch, zero);
  // Probe on and_1_out
  // Probe on or_1_out
  Adder #(.width(32)) adder_1 (.a(32'h4), .b(pc), .out(pc_plus4), .cin(1'b0));  // open: cout
  Adder #(.width(32)) adder_2 (.a(pc), .b(immediate), .out(adder_2_out), .cin(1'b0));  // open: cout
  or or_1 (or_1_out, and_1_out, jump);
  Multiplexer #(.width(32), .enable("false")) multiplexer_1 (
    .in0(pc_plus4), .in1(adder_2_out), .out(next_pc), .sel(or_1_out));
endmodule

module CPU_Top (
  input  clock
);

  wire alu_1_zero, main_control_1_alusrc, main_control_1_branch, main_control_1_jump, main_control_1_memread,
       main_control_1_memwrite, main_control_1_regwrite;
  wire [1:0] alu_control_1_alu_control, main_control_1_alu_op, main_control_1_immsel,
       main_control_1_resultsrc;
  wire [2:0] instruction_splitter_1_funct3;
  wire [4:0] instruction_splitter_1_rd, instruction_splitter_1_rs1, instruction_splitter_1_rs2;
  wire [6:0] instruction_splitter_1_funct7, instruction_splitter_1_opcode;
  wire [31:0] alu_1_alu_result, branch_jump_logic_1_next_pc, branch_jump_logic_1_pc_plus4,
       data_memory_1_read_data, immediate_generator_1_immediate, instruction_memory_1_instruction,
       multiplexer_1_out, multiplexer_2_out, program_counter_1_pc, register_file_1_read_data_1,
       register_file_1_read_data_2;

  // Probe on branch_jump_logic_1_next_pc
  program_counter program_counter_1 (.next_pc(branch_jump_logic_1_next_pc), .clock(clock), .pc(program_counter_1_pc));
  // Probe on program_counter_1_pc[6:2]
  Instruction_Memory instruction_memory_1 (
    .instruction_address(program_counter_1_pc[6:2]), .instruction(instruction_memory_1_instruction));
  Instruction_splitter instruction_splitter_1 (
    .instruction(instruction_memory_1_instruction), .opcode(instruction_splitter_1_opcode),
    .rd(instruction_splitter_1_rd), .funct3(instruction_splitter_1_funct3), .rs1(instruction_splitter_1_rs1),
    .rs2(instruction_splitter_1_rs2), .funct7(instruction_splitter_1_funct7));
  Main_control main_control_1 (
    .opcode(instruction_splitter_1_opcode), .RegWrite(main_control_1_regwrite),
    .ALUSrc(main_control_1_alusrc), .memread(main_control_1_memread), .MemWrite(main_control_1_memwrite),
    .Branch(main_control_1_branch), .jump(main_control_1_jump), .ResultSrc(main_control_1_resultsrc),
    .immsel(main_control_1_immsel), .ALU_OP(main_control_1_alu_op));  // open: is_R_type, is_ADDI, is_LW, is_SW, is_BEQ, is_JAL
  Register_File register_file_1 (
    .write_data(multiplexer_2_out), .reg_write(main_control_1_regwrite), .clock(clock),
    .read_address_1(instruction_splitter_1_rs1), .write_address(instruction_splitter_1_rd),
    .read_address_2(instruction_splitter_1_rs2), .read_data_1(register_file_1_read_data_1),
    .read_data_2(register_file_1_read_data_2));
  ALU_Control alu_control_1 (
    .ALUOp(main_control_1_alu_op), .funct3(instruction_splitter_1_funct3),
    .funct7(instruction_splitter_1_funct7), .ALU_Control(alu_control_1_alu_control));  // open: R_SUB, ALUControl_0, R_AND, ALUControl_1, R_OR
  Multiplexer #(.width(32), .enable("false")) multiplexer_1 (
    .in0(register_file_1_read_data_2), .in1(immediate_generator_1_immediate), .out(multiplexer_1_out),
    .sel(main_control_1_alusrc));
  ALU alu_1 (
    .ALU_CONTROL(alu_control_1_alu_control), .ALU_result(alu_1_alu_result), .B(multiplexer_1_out),
    .A(register_file_1_read_data_1), .ZERO(alu_1_zero));
  Multiplexer #(.select(2), .width(32), .enable("false")) multiplexer_2 (
    .in0(alu_1_alu_result), .in1(data_memory_1_read_data), .in2(branch_jump_logic_1_pc_plus4),
    .in3({32{1'b0}}), .out(multiplexer_2_out), .sel(main_control_1_resultsrc));
  Immediate_Generator immediate_generator_1 (
    .instruction(instruction_memory_1_instruction), .imm_sel(main_control_1_immsel),
    .immediate(immediate_generator_1_immediate));
  data_memory data_memory_1 (
    .address(alu_1_alu_result), .write_data(register_file_1_read_data_2), .Memwrite(main_control_1_memwrite),
    .clock(clock), .Memread(main_control_1_memread), .read_data(data_memory_1_read_data));
  Branch_Jump_Logic branch_jump_logic_1 (
    .pc(program_counter_1_pc), .immediate(immediate_generator_1_immediate), .Branch(main_control_1_branch),
    .zero(alu_1_zero), .jump(main_control_1_jump), .next_pc(branch_jump_logic_1_next_pc),
    .pc_plus4(branch_jump_logic_1_pc_plus4));
endmodule
